# Fritzing sketch PoolTechClimateControl-DT-J2H3DK3 (saved by Fritzing 0.9.10b)
breadboards: 2

parts:
  HLK-PM1 = HLK-PM01
  Arduino_Nano = Arduino Nano (Rev3.0) (ICSP)
  DHT4 = DHT22 Humidity and Temperature Sensor
  DHT3 = DHT22 Humidity and Temperature Sensor
  DHT2 = DHT22 Humidity and Temperature Sensor
  DHT1 = DHT22 Humidity and Temperature Sensor
  Real_time_clock = Tiny RTC - DS1307 Breakout Board
  R1 = Resistor [tolerance=±5% power=0.25 resistance=10k package=THT]
  R2 = Resistor [tolerance=±5% power=0.25 resistance=10k package=THT]
  R3 = Resistor [tolerance=±5% power=0.25 resistance=10k package=THT]
  R4 = Resistor [tolerance=±5% power=0.25 resistance=10k package=THT]
  Error = smd LED [color="Red (635nm)" package="0603 [SMD]"]
  Power = smd LED [color="Green (570nm)" package="0603 [SMD]"]
  R5 = Resistor [tolerance=±5% power=0.25 resistance=570 package=THT]
  R6 = Resistor [tolerance=±5% power=0.25 resistance=570 package=THT]
  LCD_on/off = Pushbutton [package="[THT]"]
  SD_card_adapter = MicroSD Card Adapter [part_number=HW-125]
  LCD2004-I2C1_20x4 = LCD2004-I2C
  C2 = Electrolytic Capacitor [capacitance=1mF voltage=35V package="100 mil [THT, electrolytic]"]
  KF-301_Relais = KF-301 Relay [package=THT]
  Fan = Fan - Ventilador [package=THT]
  Part3 = Lilypad Battery Connect  # not connected
  Part4 = Lilypad Battery Connect  # not connected
  J1 = Camdenboss CTB0158-3 [part_number=CTB0158-3 package=THT]

nets:
  N1: HLK-PM1.AC#0, Fan.N, J1.pin2
  N2: HLK-PM1.AC#1, KF-301_Relais.C, J1.pin3
  GND: HLK-PM1.-Vo, Arduino_Nano.GND, DHT4.GND, DHT3.GND, DHT2.GND, DHT1.GND, Real_time_clock.GND, R5.Pin_0, R6.Pin_0, LCD_on/off.Pin_3, LCD_on/off.Pin_4, SD_card_adapter.GND, LCD2004-I2C1_20x4.GND, C2.-, KF-301_Relais.ground
  VDD: HLK-PM1.+Vo, Arduino_Nano.5V, DHT4.VDD, DHT3.VDD, DHT2.VDD, DHT1.VDD, Real_time_clock.VCC, R1.Pin_0, R2.Pin_0, R3.Pin_0, R4.Pin_0, Power.anode, SD_card_adapter.VCC, LCD2004-I2C1_20x4.VCC, C2.+, KF-301_Relais.power
  N3: Arduino_Nano.D3, LCD_on/off.Pin_1, LCD_on/off.Pin_2
  N4: Arduino_Nano.D4, DHT1.DATA, R4.Pin_1
  N5: Arduino_Nano.D5, DHT2.DATA, R3.Pin_1
  N6: Arduino_Nano.D6, KF-301_Relais.signal
  N7: Arduino_Nano.D7, DHT3.DATA, R2.Pin_1
  N8: Arduino_Nano.D8, DHT4.DATA, R1.Pin_1
  N9: Arduino_Nano.D9, Error.anode
  N10: Arduino_Nano.D10, SD_card_adapter.CS
  N11: Arduino_Nano.D11/MOSI, SD_card_adapter.MOSI
  N12: Arduino_Nano.D12/MISO, SD_card_adapter.MISO
  N13: Arduino_Nano.A5, Real_time_clock.SCL, LCD2004-I2C1_20x4.SCL
  N14: Arduino_Nano.A4, Real_time_clock.SDA, LCD2004-I2C1_20x4.SDA
  N15: Arduino_Nano.D13/SCK, SD_card_adapter.SCK
  N16: Error.cathode, R5.Pin_1
  N17: Power.cathode, R6.Pin_1
  N18: KF-301_Relais.NO, Fan.P

notes:
  DHT1 & DHT2: inside
  DHT2 & DHT3: outside
  ~230V

custom parts:
  Tiny RTC - DS1307 Breakout Board: The Tiny RTC is a breakout board for the Dallas Semiconductor/Maxim Integrated DS1307 real-time clock. The DS1307 counts seconds, minutes, hours, date of the month, month, day of the week, and year (with compensation for leap-years). The breakout board also has space for a DS18B20 digital thermometer.
  MicroSD Card Adapter: SPI Reader Micro memory SD TF card Memory Card Shield Module *Easy and inexpensive expansion of your Arduino memory using SD card slot * Easy communication By SPI protocol * Support Micro SD Card(2G), Micro SDHC card (32G)(high-speed card) * Supports 5V
  LCD2004-I2C: A standard character display with 4x20 characters. Comes in many colors with LCM2004 IIC attached.
  KF-301 Relay: KF-301
  Fan - Ventilador: Ventilador de 2 pines, se encuentra comunmente en computadoras de escritorio
